// Digital circuit CPU_ALU.dig as structural Verilog
module CPU_ALU (
  input  [2:0] Op,
  input  [7:0] A,
  input  [7:0] B,
  output gt,
  output eq__eq,
  output lt,
  output [7:0] Result
);

  wire decoder_1_out_0, decoder_1_out_1, decoder_1_out_2, decoder_1_out_3, decoder_1_out_4, decoder_1_out_5,
       decoder_1_out_6, decoder_1_out_7;
  wire [7:0] cpu_addermultiplier_1_p, cpu_fulladder_8bits_1_sum, cpu_fullsub_8bits_1_diff_8bits,
       cpu_leftbitshift_8bits_1_a_shifted, cpu_selector_8bits_1_out, cpu_selector_8bits_2_out,
       cpu_selector_8bits_3_out, cpu_selector_8bits_4_out, cpu_selector_8bits_5_out,
       cpu_selector_8bits_6_out, cpu_selector_8bits_7_out, cpu_selector_8bits_9_out,
       cpu_selector_8bits_10_out;

  Decoder #(.Selector_Bits(3)) decoder_1 (
    .sel(Op), .out_0(decoder_1_out_0), .out_1(decoder_1_out_1), .out_2(decoder_1_out_2),
    .out_3(decoder_1_out_3), .out_4(decoder_1_out_4), .out_5(decoder_1_out_5), .out_6(decoder_1_out_6),
    .out_7(decoder_1_out_7));
  LED NullOP (.in(decoder_1_out_7));
  LED NullOP_2 (.in(decoder_1_out_6));
  LED NullOP_3 (.in(decoder_1_out_5));
  CPU_Selector_8bits cpu_selector_8bits_1 (
    .Num_Select(A), .Enable_Select(decoder_1_out_0), .Out(cpu_selector_8bits_1_out));
  CPU_Selector_8bits cpu_selector_8bits_2 (
    .Num_Select(B), .Enable_Select(decoder_1_out_0), .Out(cpu_selector_8bits_2_out));
  CPU_Selector_8bits cpu_selector_8bits_3 (
    .Num_Select(A), .Enable_Select(decoder_1_out_1), .Out(cpu_selector_8bits_3_out));
  CPU_Selector_8bits cpu_selector_8bits_4 (
    .Num_Select(B), .Enable_Select(decoder_1_out_1), .Out(cpu_selector_8bits_4_out));
  CPU_Selector_8bits cpu_selector_8bits_5 (
    .Num_Select(A), .Enable_Select(decoder_1_out_2), .Out(cpu_selector_8bits_5_out));
  CPU_Selector_8bits cpu_selector_8bits_6 (
    .Num_Select(B), .Enable_Select(decoder_1_out_2), .Out(cpu_selector_8bits_6_out));
  CPU_Selector_8bits cpu_selector_8bits_7 (
    .Num_Select(A), .Enable_Select(decoder_1_out_3), .Out(cpu_selector_8bits_7_out));
  CPU_Selector_8bits cpu_selector_8bits_8 (.Num_Select(B), .Enable_Select(decoder_1_out_3));  // open: Out
  CPU_Selector_8bits cpu_selector_8bits_9 (
    .Num_Select(A), .Enable_Select(decoder_1_out_4), .Out(cpu_selector_8bits_9_out));
  CPU_Selector_8bits cpu_selector_8bits_10 (
    .Num_Select(B), .Enable_Select(decoder_1_out_4), .Out(cpu_selector_8bits_10_out));
  CPU_FullAdder_8bits cpu_fulladder_8bits_1 (
    .A_8Bits(cpu_selector_8bits_1_out), .B_8Bits(cpu_selector_8bits_2_out), .C_in(1'b0),
    .Sum(cpu_fulladder_8bits_1_sum));  // open: C_out
  CPU_FullSub_8bits cpu_fullsub_8bits_1 (
    .A_8bits(cpu_selector_8bits_3_out), .B_8bits(cpu_selector_8bits_4_out),
    .Diff_8bits(cpu_fullsub_8bits_1_diff_8bits));  // open: Borrow_out_8Bits
  CPU_ComparatorMinusOne_8bits cpu_comparatorminusone_8bits_1 (
    .A_8bits(cpu_selector_8bits_5_out), .B_8bits(cpu_selector_8bits_6_out), .Greater(gt), .Equal(eq__eq),
    .Lesser(lt));
  CPU_LeftBitShift_8bits cpu_leftbitshift_8bits_1 (
    .Shift(1'b1), .A(cpu_selector_8bits_7_out), .A_Shifted(cpu_leftbitshift_8bits_1_a_shifted));
  CPU_AdderMultiplier cpu_addermultiplier_1 (
    .A(cpu_selector_8bits_9_out), .B(cpu_selector_8bits_10_out), .P(cpu_addermultiplier_1_p));
  Multiplexer #(.Selector_Bits(3), .Bits(8)) multiplexer_1 (
    .sel(Op), .in_0(cpu_fulladder_8bits_1_sum), .in_1(cpu_fullsub_8bits_1_diff_8bits), .in_2({8{1'b0}}),
    .in_3(cpu_leftbitshift_8bits_1_a_shifted), .in_4(cpu_addermultiplier_1_p), .in_5({8{1'b0}}),
    .in_6({8{1'b0}}), .in_7({8{1'b0}}), .out(Result));

  // Notes on the sheet:
  //   A: Entrada de 8bits de dados
  //   B: Entrada de 8bits de dados
  //   OpCode:
  //   000 - SOMA
  //   001 - SUB
  //   010 - COMPARAÇÃO
  //   011 - LEFT BIT SHIFT
  //   100 - MULTIPLICAÇÃO 4Bits
  //   101/110/111 - NULL
  //   Difference
endmodule
