// Digital circuit CPU_Display.dig as structural Verilog
module CPU_Display (
  input  [2:0] OpCode,
  input  [7:0] A,
  input  [7:0] B,
  input  clk,
  output [7:0] Debug
);

  wire cpu_alu_1_eq__eq, cpu_alu_1_gt, cpu_alu_1_lt;
  wire [7:0] cpu_alu_1_result;

  CPU_ALU cpu_alu_1 (
    .Op(OpCode), .A(A), .B(B), .gt(cpu_alu_1_gt), .eq__eq(cpu_alu_1_eq__eq), .lt(cpu_alu_1_lt),
    .Result(cpu_alu_1_result));
  LED Greater____gt (.in(cpu_alu_1_gt));
  LED Equal____eq__eq (.in(cpu_alu_1_eq__eq));
  LED Lesser____lt (.in(cpu_alu_1_lt));
  Register #(.Bits(8)) register_1 (.D(cpu_alu_1_result), .C(clk), .en(1'b1), .Q(Debug));
  Seven_Seg_Hex seven_seg_hex_1 (.d(Debug[7:4]), .dp(1'b0));
  Seven_Seg_Hex seven_seg_hex_2 (.d(Debug[3:0]), .dp(1'b1));

  // Notes on the sheet:
  //   OpCode:
  //   000 - SOMA
  //   001 - SUB
  //   010 - COMPARAÇÃO
  //   011 - LEFT BIT SHIFT
  //   100 - MULTIPLICAÇÃO 4Bits
  //   101/110/111 - NULL
endmodule
