// Digital circuit CPU_FullAdder_8bits.dig as structural Verilog
module CPU_FullAdder_8bits (
  input  [7:0] A_8Bits,
  input  [7:0] B_8Bits,
  input  C_in,
  output [7:0] Sum,
  output C_out
);

  wire cpu_fulladder_1_c_out, cpu_fulladder_2_c_out, cpu_fulladder_3_c_out, cpu_fulladder_4_c_out,
       cpu_fulladder_5_c_out, cpu_fulladder_6_c_out, cpu_fulladder_7_c_out;

  CPU_FullAdder cpu_fulladder_1 (
    .A(A_8Bits[0]), .B(B_8Bits[0]), .C_in(C_in), .Sum(Sum[0]), .C_out(cpu_fulladder_1_c_out));
  CPU_FullAdder cpu_fulladder_2 (
    .A(A_8Bits[1]), .B(B_8Bits[1]), .C_in(cpu_fulladder_1_c_out), .Sum(Sum[1]), .C_out(cpu_fulladder_2_c_out));
  CPU_FullAdder cpu_fulladder_3 (
    .A(A_8Bits[2]), .B(B_8Bits[2]), .C_in(cpu_fulladder_2_c_out), .Sum(Sum[2]), .C_out(cpu_fulladder_3_c_out));
  CPU_FullAdder cpu_fulladder_4 (
    .A(A_8Bits[3]), .B(B_8Bits[3]), .C_in(cpu_fulladder_3_c_out), .Sum(Sum[3]), .C_out(cpu_fulladder_4_c_out));
  CPU_FullAdder cpu_fulladder_5 (
    .A(A_8Bits[4]), .B(B_8Bits[4]), .C_in(cpu_fulladder_4_c_out), .Sum(Sum[4]), .C_out(cpu_fulladder_5_c_out));
  CPU_FullAdder cpu_fulladder_6 (
    .A(A_8Bits[5]), .B(B_8Bits[5]), .C_in(cpu_fulladder_5_c_out), .Sum(Sum[5]), .C_out(cpu_fulladder_6_c_out));
  CPU_FullAdder cpu_fulladder_7 (
    .A(A_8Bits[6]), .B(B_8Bits[6]), .C_in(cpu_fulladder_6_c_out), .Sum(Sum[6]), .C_out(cpu_fulladder_7_c_out));
  CPU_FullAdder cpu_fulladder_8 (
    .A(A_8Bits[7]), .B(B_8Bits[7]), .C_in(cpu_fulladder_7_c_out), .Sum(Sum[7]), .C_out(C_out));
endmodule
