// Digital circuit ex_5.03.dig as structural Verilog
module ex_5_03 (
  input  X,
  input  Y,
  input  Z,
  output F3
);

  wire not_1_out, not_2_out, or_1_out;

  not not_1 (not_1_out, X);
  not not_2 (not_2_out, Y);
  or or_1 (or_1_out, not_1_out, not_2_out);
  and and_1 (F3, or_1_out, Z);
endmodule
