// Digital circuit CPU_ComparatorMinusOne.dig as structural Verilog
module CPU_ComparatorMinusOne (
  input  A,
  input  B,
  input  _1__eq,
  output Greater,
  output Equal,
  output Lesser
);

  wire and_2_out, and_3_out, not_1_out, not_2_out;

  not not_1 (not_1_out, B);
  not not_2 (not_2_out, A);
  and and_1 (Greater, A, _1__eq, not_1_out);
  and and_2 (and_2_out, not_1_out, _1__eq, not_2_out);
  and and_3 (and_3_out, A, _1__eq, B);
  and and_4 (Lesser, not_2_out, _1__eq, B);
  or or_1 (Equal, and_2_out, and_3_out);
endmodule
