// Digital circuit CPU_FullSub_8bits.dig as structural Verilog
module CPU_FullSub_8bits (
  input  [7:0] A_8bits,
  input  [7:0] B_8bits,
  output [7:0] Borrow_out_8Bits,
  output [7:0] Diff_8bits
);

  wire [7:0] not_1_out;

  assign not_1_out = ~B_8bits;  // Not not_1, 8 bits wide
  // CPU_FullAdder_8bits cpu_fulladder_8bits_1: pin names not known; wires that end beside it: A_8bits, not_1_out, 1'b1, Diff_8bits, Borrow_out_8Bits
endmodule
