// Digital circuit CPU_LeftBitShift.dig as structural Verilog
module CPU_LeftBitShift (
  input  Shift,
  input  Bit_3,
  input  Bit_2,
  input  Bit_1,
  input  Bit_0,
  input  Bit_6,
  input  Bit_5,
  input  Bit_4,
  input  Bit_7,
  output Out_3,
  output Out_2,
  output Out_1,
  output Out_0,
  output Out_6,
  output Out_5,
  output Out_4,
  output Out_7
);

  wire and_1_out, and_2_out, and_3_out, and_4_out, and_5_out, and_6_out, and_7_out, and_8_out, and_9_out,
       and_10_out, and_11_out, and_12_out, and_13_out, and_14_out, and_15_out, and_16_out, not_1_out,
       not_2_out, not_3_out, not_4_out, not_5_out, not_6_out, not_7_out, not_8_out;

  not not_1 (not_1_out, Shift);
  and and_1 (and_1_out, Bit_7, not_1_out);
  or or_1 (Out_7, and_2_out, and_1_out);
  and and_2 (and_2_out, Bit_6, Shift);
  not not_2 (not_2_out, Shift);
  and and_3 (and_3_out, Bit_6, not_2_out);
  or or_2 (Out_6, and_4_out, and_3_out);
  and and_4 (and_4_out, Bit_5, Shift);
  not not_3 (not_3_out, Shift);
  and and_5 (and_5_out, Bit_5, not_3_out);
  or or_3 (Out_5, and_6_out, and_5_out);
  and and_6 (and_6_out, Bit_4, Shift);
  not not_4 (not_4_out, Shift);
  and and_7 (and_7_out, Bit_4, not_4_out);
  and and_8 (and_8_out, Bit_3, Shift);
  or or_4 (Out_4, and_8_out, and_7_out);
  not not_5 (not_5_out, Shift);
  and and_9 (and_9_out, Bit_3, not_5_out);
  or or_5 (Out_3, and_10_out, and_9_out);
  and and_10 (and_10_out, Bit_2, Shift);
  not not_6 (not_6_out, Shift);
  and and_11 (and_11_out, Bit_2, not_6_out);
  or or_6 (Out_2, and_12_out, and_11_out);
  and and_12 (and_12_out, Bit_1, Shift);
  not not_7 (not_7_out, Shift);
  and and_13 (and_13_out, Bit_1, not_7_out);
  or or_7 (Out_1, and_14_out, and_13_out);
  and and_14 (and_14_out, Bit_0, Shift);
  not not_8 (not_8_out, Shift);
  and and_15 (and_15_out, Bit_0, not_8_out);
  and and_16 (and_16_out, 1'b0, Shift);
  or or_8 (Out_0, and_16_out, and_15_out);
endmodule
