// Digital circuit CPU_MagComparator.dig as structural Verilog
module CPU_MagComparator (
  input  A,
  input  B,
  output Greater,
  output Equal,
  output Lesser
);

  wire not_1_out, not_2_out;

  not not_1 (not_1_out, B);
  not not_2 (not_2_out, A);
  and and_1 (Greater, A, not_1_out);
  xnor xnor_1 (Equal, A, B);
  and and_2 (Lesser, not_2_out, B);
endmodule
