// Digital circuit CPU_Selector_8bits.dig as structural Verilog
module CPU_Selector_8bits (
  input  [7:0] Num_Select,
  input  Enable_Select,
  output [7:0] Out
);

  and and_1 (Out[0], Enable_Select, Num_Select[0]);
  and and_2 (Out[1], Enable_Select, Num_Select[1]);
  and and_3 (Out[2], Enable_Select, Num_Select[2]);
  and and_4 (Out[3], Enable_Select, Num_Select[3]);
  and and_5 (Out[4], Enable_Select, Num_Select[4]);
  and and_6 (Out[5], Enable_Select, Num_Select[5]);
  and and_7 (Out[6], Enable_Select, Num_Select[6]);
  and and_8 (Out[7], Enable_Select, Num_Select[7]);

  // Other names for the same wires on the sheet: Es = Enable_Select
endmodule
