// Digital circuit ex_5.04.dig as structural Verilog
module ex_5_04 (
  input  R,
  input  S,
  input  T,
  input  U,
  output OUT
);

  wire and_1_out, and_2_out, and_3_out, and_4_out, and_5_out, and_6_out, not_1_out, not_2_out, or_1_out;

  not not_1 (not_1_out, T);
  and and_1 (and_1_out, R, S);
  and and_2 (and_2_out, S, not_1_out);
  not not_2 (not_2_out, U);
  and and_3 (and_3_out, and_1_out, U);
  and and_4 (and_4_out, and_2_out, not_2_out);
  and and_5 (and_5_out, not_1_out, R);
  and and_6 (and_6_out, and_4_out, and_5_out);
  or or_1 (or_1_out, and_3_out, and_4_out);
  or or_2 (OUT, or_1_out, and_6_out);
endmodule
