// Digital circuit CPU_AdderMultiplier.dig as structural Verilog
module CPU_AdderMultiplier (
  input  [7:0] A,
  input  [7:0] B,
  output [7:0] P
);

  wire and_1_out, and_2_out, and_3_out, and_4_out, and_5_out, and_6_out, and_7_out, and_8_out, and_9_out,
       and_10_out, and_11_out, and_12_out, and_13_out, and_14_out, and_15_out, cpu_fulladder_2_c_out,
       cpu_fulladder_2_sum, cpu_fulladder_3_c_out, cpu_fulladder_4_c_out, cpu_fulladder_4_sum,
       cpu_fulladder_5_c_out, cpu_fulladder_5_sum, cpu_fulladder_6_c_out, cpu_fulladder_7_c_out,
       cpu_fulladder_7_sum, cpu_fulladder_8_c_out, cpu_fulladder_8_sum, cpu_fulladder_9_c_out,
       cpu_fulladder_10_c_out, cpu_fulladder_10_sum, cpu_fulladder_11_c_out, cpu_fulladder_12_c_out;

  and and_1 (and_1_out, A[3], B[3]);
  CPU_FullAdder cpu_fulladder_1 (
    .A(cpu_fulladder_3_c_out), .B(and_1_out), .C_in(cpu_fulladder_2_c_out), .Sum(P[6]), .C_out(P[7]));
  and and_2 (and_2_out, A[3], B[2]);
  CPU_FullAdder cpu_fulladder_2 (
    .A(cpu_fulladder_5_c_out), .B(and_2_out), .C_in(cpu_fulladder_4_c_out), .Sum(cpu_fulladder_2_sum),
    .C_out(cpu_fulladder_2_c_out));
  and and_3 (and_3_out, A[2], B[3]);
  CPU_FullAdder cpu_fulladder_3 (
    .A(cpu_fulladder_2_sum), .B(and_3_out), .C_in(cpu_fulladder_6_c_out), .Sum(P[5]),
    .C_out(cpu_fulladder_3_c_out));
  and and_4 (and_4_out, A[3], B[1]);
  CPU_FullAdder cpu_fulladder_4 (
    .A(cpu_fulladder_7_c_out), .B(and_4_out), .C_in(1'b0), .Sum(cpu_fulladder_4_sum),
    .C_out(cpu_fulladder_4_c_out));
  and and_5 (and_5_out, A[2], B[2]);
  CPU_FullAdder cpu_fulladder_5 (
    .A(cpu_fulladder_4_sum), .B(and_5_out), .C_in(cpu_fulladder_8_c_out), .Sum(cpu_fulladder_5_sum),
    .C_out(cpu_fulladder_5_c_out));
  and and_6 (and_6_out, A[1], B[3]);
  CPU_FullAdder cpu_fulladder_6 (
    .A(cpu_fulladder_5_sum), .B(and_6_out), .C_in(cpu_fulladder_9_c_out), .Sum(P[4]),
    .C_out(cpu_fulladder_6_c_out));
  and and_7 (and_7_out, B[0], A[3]);
  and and_8 (and_8_out, A[2], B[1]);
  CPU_FullAdder cpu_fulladder_7 (
    .A(and_7_out), .B(and_8_out), .C_in(cpu_fulladder_10_c_out), .Sum(cpu_fulladder_7_sum),
    .C_out(cpu_fulladder_7_c_out));
  and and_9 (and_9_out, A[1], B[2]);
  CPU_FullAdder cpu_fulladder_8 (
    .A(cpu_fulladder_7_sum), .B(and_9_out), .C_in(cpu_fulladder_11_c_out), .Sum(cpu_fulladder_8_sum),
    .C_out(cpu_fulladder_8_c_out));
  and and_10 (and_10_out, A[0], B[3]);
  CPU_FullAdder cpu_fulladder_9 (
    .A(cpu_fulladder_8_sum), .B(and_10_out), .C_in(1'b0), .Sum(P[3]), .C_out(cpu_fulladder_9_c_out));
  and and_11 (and_11_out, A[1], B[1]);
  CPU_FullAdder cpu_fulladder_10 (
    .A(and_13_out), .B(and_11_out), .C_in(cpu_fulladder_12_c_out), .Sum(cpu_fulladder_10_sum),
    .C_out(cpu_fulladder_10_c_out));
  and and_12 (and_12_out, A[0], B[2]);
  CPU_FullAdder cpu_fulladder_11 (
    .A(cpu_fulladder_10_sum), .B(and_12_out), .C_in(1'b0), .Sum(P[2]), .C_out(cpu_fulladder_11_c_out));
  and and_13 (and_13_out, B[0], A[2]);
  and and_14 (and_14_out, B[0], A[1]);
  and and_15 (and_15_out, A[0], B[1]);
  CPU_FullAdder cpu_fulladder_12 (
    .A(and_14_out), .B(and_15_out), .C_in(1'b0), .Sum(P[1]), .C_out(cpu_fulladder_12_c_out));
  and and_16 (P[0], B[0], A[0]);
  // also tied to GND on the sheet: {A[4], A[5], A[6], A[7], B[4], B[5], B[6], B[7]}
endmodule
