// Digital circuit CPU_ComparatorMinusOne_8bits.dig as structural Verilog
module CPU_ComparatorMinusOne_8bits (
  input  [7:0] A_8bits,
  input  [7:0] B_8bits,
  output Greater,
  output Equal,
  output Lesser
);

  wire cpu_comparatorminusone_1_equal, cpu_comparatorminusone_1_greater, cpu_comparatorminusone_1_lesser,
       cpu_comparatorminusone_2_equal, cpu_comparatorminusone_2_greater, cpu_comparatorminusone_2_lesser,
       cpu_comparatorminusone_3_equal, cpu_comparatorminusone_3_greater, cpu_comparatorminusone_3_lesser,
       cpu_comparatorminusone_4_equal, cpu_comparatorminusone_4_greater, cpu_comparatorminusone_4_lesser,
       cpu_comparatorminusone_5_equal, cpu_comparatorminusone_5_greater, cpu_comparatorminusone_5_lesser,
       cpu_comparatorminusone_6_equal, cpu_comparatorminusone_6_greater, cpu_comparatorminusone_6_lesser,
       cpu_comparatorminusone_7_equal, cpu_comparatorminusone_7_greater, cpu_comparatorminusone_7_lesser,
       cpu_comparatorminusone_8_greater, cpu_comparatorminusone_8_lesser;

  CPU_ComparatorMinusOne cpu_comparatorminusone_1 (
    .A(A_8bits[7]), .B(B_8bits[7]), ._1__eq(1'b1), .Greater(cpu_comparatorminusone_1_greater),
    .Equal(cpu_comparatorminusone_1_equal), .Lesser(cpu_comparatorminusone_1_lesser));
  CPU_ComparatorMinusOne cpu_comparatorminusone_2 (
    .A(A_8bits[6]), .B(B_8bits[6]), ._1__eq(cpu_comparatorminusone_1_equal),
    .Greater(cpu_comparatorminusone_2_greater), .Equal(cpu_comparatorminusone_2_equal),
    .Lesser(cpu_comparatorminusone_2_lesser));
  CPU_ComparatorMinusOne cpu_comparatorminusone_3 (
    .A(A_8bits[5]), .B(B_8bits[5]), ._1__eq(cpu_comparatorminusone_2_equal),
    .Greater(cpu_comparatorminusone_3_greater), .Equal(cpu_comparatorminusone_3_equal),
    .Lesser(cpu_comparatorminusone_3_lesser));
  CPU_ComparatorMinusOne cpu_comparatorminusone_4 (
    .A(A_8bits[4]), .B(B_8bits[4]), ._1__eq(cpu_comparatorminusone_3_equal),
    .Greater(cpu_comparatorminusone_4_greater), .Equal(cpu_comparatorminusone_4_equal),
    .Lesser(cpu_comparatorminusone_4_lesser));
  CPU_ComparatorMinusOne cpu_comparatorminusone_5 (
    .A(A_8bits[3]), .B(B_8bits[3]), ._1__eq(cpu_comparatorminusone_4_equal),
    .Greater(cpu_comparatorminusone_5_greater), .Equal(cpu_comparatorminusone_5_equal),
    .Lesser(cpu_comparatorminusone_5_lesser));
  CPU_ComparatorMinusOne cpu_comparatorminusone_6 (
    .A(A_8bits[2]), .B(B_8bits[2]), ._1__eq(cpu_comparatorminusone_5_equal),
    .Greater(cpu_comparatorminusone_6_greater), .Equal(cpu_comparatorminusone_6_equal),
    .Lesser(cpu_comparatorminusone_6_lesser));
  CPU_ComparatorMinusOne cpu_comparatorminusone_7 (
    .A(A_8bits[1]), .B(B_8bits[1]), ._1__eq(cpu_comparatorminusone_6_equal),
    .Greater(cpu_comparatorminusone_7_greater), .Equal(cpu_comparatorminusone_7_equal),
    .Lesser(cpu_comparatorminusone_7_lesser));
  CPU_ComparatorMinusOne cpu_comparatorminusone_8 (
    .A(A_8bits[0]), .B(B_8bits[0]), ._1__eq(cpu_comparatorminusone_7_equal),
    .Greater(cpu_comparatorminusone_8_greater), .Equal(Equal), .Lesser(cpu_comparatorminusone_8_lesser));
  or or_1 (Greater, cpu_comparatorminusone_1_greater, cpu_comparatorminusone_2_greater, cpu_comparatorminusone_3_greater, cpu_comparatorminusone_4_greater, cpu_comparatorminusone_5_greater, cpu_comparatorminusone_6_greater, cpu_comparatorminusone_7_greater, cpu_comparatorminusone_8_greater);
  or or_2 (Lesser, cpu_comparatorminusone_1_lesser, cpu_comparatorminusone_2_lesser, cpu_comparatorminusone_3_lesser, cpu_comparatorminusone_4_lesser, cpu_comparatorminusone_5_lesser, cpu_comparatorminusone_6_lesser, cpu_comparatorminusone_7_lesser, cpu_comparatorminusone_8_lesser);
endmodule
