// Digital circuit CPU_LeftBitShift_8bits.dig as structural Verilog
module CPU_LeftBitShift_8bits (
  input  Shift,
  input  [7:0] A,
  output [7:0] A_Shifted
);

  wire and_1_out, and_2_out, and_3_out, and_4_out, and_5_out, and_6_out, and_7_out, and_8_out, and_9_out,
       and_10_out, and_11_out, and_12_out, and_13_out, and_14_out, and_15_out, and_16_out, not_1_out,
       not_2_out, not_3_out, not_4_out, not_5_out, not_6_out, not_7_out, not_8_out;

  not not_1 (not_1_out, Shift);
  and and_1 (and_1_out, A[7], not_1_out);
  or or_1 (A_Shifted[7], and_2_out, and_1_out);
  and and_2 (and_2_out, A[6], Shift);
  not not_2 (not_2_out, Shift);
  and and_3 (and_3_out, A[6], not_2_out);
  or or_2 (A_Shifted[6], and_4_out, and_3_out);
  and and_4 (and_4_out, A[5], Shift);
  not not_3 (not_3_out, Shift);
  and and_5 (and_5_out, A[5], not_3_out);
  or or_3 (A_Shifted[5], and_6_out, and_5_out);
  and and_6 (and_6_out, A[4], Shift);
  not not_4 (not_4_out, Shift);
  and and_7 (and_7_out, A[4], not_4_out);
  and and_8 (and_8_out, A[3], Shift);
  or or_4 (A_Shifted[4], and_8_out, and_7_out);
  not not_5 (not_5_out, Shift);
  and and_9 (and_9_out, A[3], not_5_out);
  or or_5 (A_Shifted[3], and_10_out, and_9_out);
  and and_10 (and_10_out, A[2], Shift);
  not not_6 (not_6_out, Shift);
  and and_11 (and_11_out, A[2], not_6_out);
  or or_6 (A_Shifted[2], and_12_out, and_11_out);
  and and_12 (and_12_out, A[1], Shift);
  not not_7 (not_7_out, Shift);
  and and_13 (and_13_out, A[1], not_7_out);
  or or_7 (A_Shifted[1], and_14_out, and_13_out);
  and and_14 (and_14_out, A[0], Shift);
  not not_8 (not_8_out, Shift);
  and and_15 (and_15_out, A[0], not_8_out);
  and and_16 (and_16_out, 1'b0, Shift);
  or or_8 (A_Shifted[0], and_16_out, and_15_out);
endmodule
